# Fritzing sketch computer (saved by Fritzing 0.9.3b)
breadboards: 1

parts:
  TC551001BPL-70L = IC, DIP package, 32 pins [chip_label=TC551001BPL-70L]
  R1 = Resistor [tolerance=±5% resistance=1k package=THT]
  R2 = Resistor [tolerance=±5% resistance=1k package=THT]
  5V_power = Power plug
  U1 = 555 Timer [package="DIP8 [THT]"]
  R3 = Trimmer Potentiometer [maximum_resistance=100kΩ package=THT]
  R3_2 = Rotary Potentiometer (Large) [maximum_resistance=20kΩ package=THT]
  R4 = Resistor [tolerance=±5% resistance=100 package=THT]
  C1 = Electrolytic Capacitor [capacitance=47µF package="100 mil [THT, electrolytic]"]
  C2 = Ceramic Capacitor [capacitance=10nF package="100 mil [THT, multilayer]"]
  R5 = Resistor [tolerance=±5% resistance=330 package=THT]
  LED1 = LED - 5mm [color="Red (633nm)" package="5 mm [THT]"]
  LED2 = LED - 5mm [color="Red (633nm)" package="5 mm [THT]"]
  R6 = Resistor [tolerance=±5% resistance=330 package=THT]
  LED3 = LED - 5mm [color="Red (633nm)" package="5 mm [THT]"]
  R7 = Resistor [tolerance=±5% resistance=330 package=THT]
  LED4 = LED - 5mm [color="Red (633nm)" package="5 mm [THT]"]
  R8 = Resistor [tolerance=±5% resistance=330 package=THT]
  LED5 = LED - 5mm [color="Red (633nm)" package="5 mm [THT]"]
  R9 = Resistor [tolerance=±5% resistance=330 package=THT]
  LED6 = LED - 5mm [color="Red (633nm)" package="5 mm [THT]"]
  LED7 = LED - 5mm [color="Red (633nm)" package="5 mm [THT]"]
  LED8 = LED - 5mm [color="Red (633nm)" package="5 mm [THT]"]
  LED9 = LED - 5mm [color="Red (633nm)" package="5 mm [THT]"]
  R10 = Resistor [tolerance=±5% resistance=330 package=THT]
  R11 = Resistor [tolerance=±5% resistance=330 package=THT]
  R12 = Resistor [tolerance=±5% resistance=330 package=THT]
  R13 = Resistor [tolerance=±5% resistance=330 package=THT]
  74HC08 = IC, DIP package, 14 pins [chip_label=74HC08]
  R14 = Resistor [tolerance=±5% resistance=1k package=THT]
  S1 = Pushbutton [package="[THT]"]
  C3 = Ceramic Capacitor [capacitance=0.1nF package="100 mil [THT, multilayer]"]
  S3 = Toggle Switch [package=THT]
  74HC08_2 = IC, DIP package, 14 pins [chip_label=74HC08]
  Z80 = IC, DIP package, 40 pins [chip_label=Z80]
  R19 = Resistor [tolerance=±5% resistance=330 package=THT]
  LED10 = LED - 5mm [color="Red (633nm)" package="5 mm [THT]"]
  R20 = Resistor [tolerance=±5% resistance=1k package=THT]
  R21 = Resistor [tolerance=±5% resistance=1k package=THT]
  R22 = Resistor [tolerance=±5% resistance=330 package=THT]
  LED11 = LED - 5mm [color="Red (633nm)" package="5 mm [THT]"]
  R23 = Resistor [tolerance=±5% resistance=330 package=THT]
  LED12 = LED - 5mm [color="Red (633nm)" package="5 mm [THT]"]
  R24 = Resistor [tolerance=±5% resistance=330 package=THT]
  LED13 = LED - 5mm [color="Red (633nm)" package="5 mm [THT]"]
  R25 = Resistor [tolerance=±5% resistance=330 package=THT]
  LED14 = LED - 5mm [color="Red (633nm)" package="5 mm [THT]"]
  R26 = Resistor [tolerance=±5% resistance=1k package=THT]
  R27 = Resistor [tolerance=±5% resistance=1k package=THT]
  R28 = Resistor [tolerance=±5% resistance=1k package=THT]
  R29 = Resistor [tolerance=±5% resistance=1k package=THT]
  R30 = Resistor [tolerance=±5% resistance=1k package=THT]
  S4 = Toggle Switch [package=THT]
  R31 = Resistor [tolerance=±5% resistance=1k package=THT]
  S5 = Toggle Switch [package=THT]
  C4 = Ceramic Capacitor [capacitance=100nF package="100 mil [THT, multilayer]"]
  C5 = Ceramic Capacitor [capacitance=100nF package="100 mil [THT, multilayer]"]
  C6 = Ceramic Capacitor [capacitance=100nF package="100 mil [THT, multilayer]"]
  C7 = Electrolytic Capacitor [capacitance=1mF package="100 mil [THT, electrolytic]"]
  C8 = Ceramic Capacitor [capacitance=100nF package="100 mil [THT, multilayer]"]
  S6 = Toggle Switch [package=THT]
  R32 = Resistor [tolerance=±5% resistance=1k package=THT]
  R33 = Resistor [tolerance=±5% resistance=330 package=THT]
  LED15 = LED - 5mm [color="Red (633nm)" package="5 mm [THT]"]
  LED16 = LED - 5mm [color="Red (633nm)" package="5 mm [THT]"]
  S7 = Toggle Switch [package=THT]
  R34 = Resistor [tolerance=±5% resistance=1k package=THT]
  R35 = Resistor [tolerance=±5% resistance=330 package=THT]
  LED17 = LED - 5mm [color="Red (633nm)" package="5 mm [THT]"]
  S8 = Toggle Switch [package=THT]
  R36 = Resistor [tolerance=±5% resistance=1k package=THT]
  R37 = Resistor [tolerance=±5% resistance=330 package=THT]
  LED18 = LED - 5mm [color="Red (633nm)" package="5 mm [THT]"]
  S9 = Toggle Switch [package=THT]
  R38 = Resistor [tolerance=±5% resistance=1k package=THT]
  R39 = Resistor [tolerance=±5% resistance=330 package=THT]
  LED19 = LED - 5mm [color="Red (633nm)" package="5 mm [THT]"]
  LED20 = LED - 5mm [color="Red (633nm)" package="5 mm [THT]"]
  LED21 = LED - 5mm [color="Red (633nm)" package="5 mm [THT]"]
  LED22 = LED - 5mm [color="Red (633nm)" package="5 mm [THT]"]
  S10 = Toggle Switch [package=THT]
  S11 = Toggle Switch [package=THT]
  S12 = Toggle Switch [package=THT]
  S13 = Toggle Switch [package=THT]
  R40 = Resistor [tolerance=±5% resistance=1k package=THT]
  R41 = Resistor [tolerance=±5% resistance=1k package=THT]
  R42 = Resistor [tolerance=±5% resistance=1k package=THT]
  R43 = Resistor [tolerance=±5% resistance=1k package=THT]
  R44 = Resistor [tolerance=±5% resistance=330 package=THT]
  R45 = Resistor [tolerance=±5% resistance=330 package=THT]
  R46 = Resistor [tolerance=±5% resistance=330 package=THT]
  R47 = Resistor [tolerance=±5% resistance=330 package=THT]
  LED23 = LED - 5mm [color="Red (633nm)" package="5 mm [THT]"]
  LED24 = LED - 5mm [color="Red (633nm)" package="5 mm [THT]"]
  LED25 = LED - 5mm [color="Red (633nm)" package="5 mm [THT]"]
  LED26 = LED - 5mm [color="Red (633nm)" package="5 mm [THT]"]
  LED27 = LED - 5mm [color="Red (633nm)" package="5 mm [THT]"]
  LED28 = LED - 5mm [color="Red (633nm)" package="5 mm [THT]"]
  LED29 = LED - 5mm [color="Red (633nm)" package="5 mm [THT]"]
  LED30 = LED - 5mm [color="Red (633nm)" package="5 mm [THT]"]
  S14 = Toggle Switch [package=THT]
  S15 = Toggle Switch [package=THT]
  S16 = Toggle Switch [package=THT]
  S17 = Toggle Switch [package=THT]
  S18 = Toggle Switch [package=THT]
  S19 = Toggle Switch [package=THT]
  S20 = Toggle Switch [package=THT]
  S21 = Toggle Switch [package=THT]
  R48 = Resistor [tolerance=±5% resistance=1k package=THT]
  R49 = Resistor [tolerance=±5% resistance=1k package=THT]
  R50 = Resistor [tolerance=±5% resistance=1k package=THT]
  R51 = Resistor [tolerance=±5% resistance=1k package=THT]
  R52 = Resistor [tolerance=±5% resistance=1k package=THT]
  R53 = Resistor [tolerance=±5% resistance=1k package=THT]
  R54 = Resistor [tolerance=±5% resistance=1k package=THT]
  R55 = Resistor [tolerance=±5% resistance=1k package=THT]
  R56 = Resistor [tolerance=±5% resistance=330 package=THT]
  R57 = Resistor [tolerance=±5% resistance=330 package=THT]
  R58 = Resistor [tolerance=±5% resistance=330 package=THT]
  R59 = Resistor [tolerance=±5% resistance=330 package=THT]
  R60 = Resistor [tolerance=±5% resistance=330 package=THT]
  R61 = Resistor [tolerance=±5% resistance=330 package=THT]
  R62 = Resistor [tolerance=±5% resistance=330 package=THT]
  R63 = Resistor [tolerance=±5% resistance=330 package=THT]
  S23 = Toggle Switch [package=THT]
  R65 = Resistor [tolerance=±5% resistance=1k package=THT]
  S24 = Toggle Switch [package=THT]
  R66 = Resistor [tolerance=±5% resistance=1k package=THT]
  S25 = Toggle Switch [package=THT]
  S26 = Toggle Switch [package=THT]
  R67 = Resistor [tolerance=±5% resistance=1k package=THT]
  R68 = Resistor [tolerance=±5% resistance=1k package=THT]
  S27 = Toggle Switch [package=THT]
  S28 = Toggle Switch [package=THT]
  S29 = Toggle Switch [package=THT]
  S30 = Toggle Switch [package=THT]
  R69 = Resistor [tolerance=±5% resistance=1k package=THT]
  R70 = Resistor [tolerance=±5% resistance=1k package=THT]
  R71 = Resistor [tolerance=±5% resistance=1k package=THT]
  R72 = Resistor [tolerance=±5% resistance=1k package=THT]

nets:
  N1: TC551001BPL-70L.pin2, R1.Pin_1
  N2: TC551001BPL-70L.pin3, Z80.pin4, S17.COM, R52.Pin_1, R58.Pin_1
  N3: TC551001BPL-70L.pin4, Z80.pin2, S16.COM, R54.Pin_1, R60.Pin_1
  N4: TC551001BPL-70L.pin5, Z80.pin37, S13.COM, R42.Pin_1, R47.Pin_1
  N5: TC551001BPL-70L.pin6, Z80.pin36, S11.COM, R41.Pin_1, R46.Pin_1
  N6: TC551001BPL-70L.pin7, Z80.pin35, S12.COM, R43.Pin_1, R45.Pin_1
  N7: TC551001BPL-70L.pin8, Z80.pin34, S10.COM, R40.Pin_1, R44.Pin_1
  N8: TC551001BPL-70L.pin9, Z80.pin33, S9.COM, R38.Pin_1, R39.Pin_1
  N9: TC551001BPL-70L.pin10, Z80.pin32, S8.COM, R36.Pin_1, R37.Pin_1
  N10: TC551001BPL-70L.pin11, Z80.pin31, S7.COM, R34.Pin_1, R35.Pin_1
  N11: TC551001BPL-70L.pin12, Z80.pin30, S6.COM, R32.Pin_1, R33.Pin_1
  N12: TC551001BPL-70L.pin13, 74HC08_2.pin2, Z80.pin14, S28.COM, R72.Pin_1
  N13: TC551001BPL-70L.pin14, 74HC08_2.pin5, Z80.pin15, S27.COM, R70.Pin_1
  N14: TC551001BPL-70L.pin15, 74HC08_2.pin9, Z80.pin12, S29.COM, R69.Pin_1
  N15: TC551001BPL-70L.pin16, R1.Pin_0, R2.Pin_0, 5V_power.GND, U1.Ground, C1.-, C2.0, LED1.cathode, S1.Pin_4, C3.0, Z80.pin29, LED11.cathode, LED12.cathode, LED13.cathode, LED14.cathode, R29.Pin_0, R30.Pin_0, C4.0, C5.1, C7.-
  N16: TC551001BPL-70L.pin17, 74HC08_2.pin12, Z80.pin8, S30.COM, R71.Pin_1
  N17: TC551001BPL-70L.pin18, 74HC08.pin2, Z80.pin7, S26.COM, R67.Pin_1
  N18: TC551001BPL-70L.pin19, 74HC08.pin5, Z80.pin9, S25.COM, R68.Pin_1
  N19: TC551001BPL-70L.pin20, 74HC08.pin9, Z80.pin10, S24.COM, R66.Pin_1
  N20: TC551001BPL-70L.pin21, 74HC08.pin12, Z80.pin13, S23.COM, R65.Pin_1
  N21: TC551001BPL-70L.pin22, R29.Pin_1
  N22: TC551001BPL-70L.pin23, Z80.pin40, S21.COM, R55.Pin_1, R62.Pin_1
  N23: TC551001BPL-70L.pin24, S3.L1, R30.Pin_1
  N24: TC551001BPL-70L.pin25, Z80.pin1, S20.COM, R50.Pin_1, R61.Pin_1
  N25: TC551001BPL-70L.pin26, Z80.pin39, S18.COM, R49.Pin_1, R57.Pin_1
  N26: TC551001BPL-70L.pin27, Z80.pin38, S14.COM, R48.Pin_1, R56.Pin_1
  N27: TC551001BPL-70L.pin28, Z80.pin3, S15.COM, R53.Pin_1, R59.Pin_1
  N28: TC551001BPL-70L.pin29, S1.Pin_1, S1.Pin_2, C3.1, Z80.pin22, R25.Pin_1, S4.COM
  N29: TC551001BPL-70L.pin30, R14.Pin_0
  N30: TC551001BPL-70L.pin31, R2.Pin_1
  N31: TC551001BPL-70L.pin32, 5V_power.VCC, U1.Reset, U1.Vcc_Supply_Voltage, R4.Pin_1, R14.Pin_1, Z80.pin11, R20.Pin_1, R21.Pin_1, R26.Pin_1, R27.Pin_1, R28.Pin_1, R31.Pin_1, S5.L1, C4.1, C5.0, C7.+, S6.L1, S7.L1, S8.L1, S9.L1, S10.L1, S11.L1, S12.L1, S13.L1, S14.L1, S15.L1, S16.L1, S17.L1, S18.L1, S19.L1, S20.L1, S21.L1, S23.L1, S24.L1, S25.L1, S26.L1, S27.L1, S28.L1, S29.L1, S30.L1
  N32: U1.Trigger, U1.Threshold, U1.Discharge, R3.wiper, R3_2.wiper, C1.+
  N33: U1.Output, R5.Pin_1, Z80.pin6
  N34: U1.Control_Voltage, C2.1
  N35: R3.leg2, R3_2.leg2, R4.Pin_0
  N36: R5.Pin_0, LED1.anode
  N37: LED2.cathode, LED3.cathode, LED4.cathode, LED5.cathode, LED6.cathode, LED7.cathode, LED8.cathode, LED9.cathode, LED10.cathode, R32.Pin_0, LED15.cathode, LED16.cathode, R34.Pin_0, LED17.cathode, R36.Pin_0, LED18.cathode, R38.Pin_0, LED19.cathode, LED20.cathode, LED21.cathode, LED22.cathode, R40.Pin_0, R41.Pin_0, R42.Pin_0, R43.Pin_0, LED23.cathode, LED24.cathode, LED25.cathode, LED26.cathode, LED27.cathode, LED28.cathode, LED29.cathode, LED30.cathode, R48.Pin_0, R49.Pin_0, R50.Pin_0, R51.Pin_0, R52.Pin_0, R53.Pin_0, R54.Pin_0, R55.Pin_0
  N38: LED2.anode, R6.Pin_1
  N39: R6.Pin_0, 74HC08_2.pin3
  N40: LED3.anode, R7.Pin_1
  N41: R7.Pin_0, 74HC08_2.pin6
  N42: LED4.anode, R8.Pin_1
  N43: R8.Pin_0, 74HC08_2.pin8
  N44: LED5.anode, R9.Pin_1
  N45: R9.Pin_0, 74HC08_2.pin11
  N46: LED6.anode, R10.Pin_1
  N47: LED7.anode, R11.Pin_1
  N48: LED8.anode, R13.Pin_1
  N49: LED9.anode, R12.Pin_1
  N50: R10.Pin_0, 74HC08.pin3
  N51: R11.Pin_0, 74HC08.pin8
  N52: R12.Pin_0, 74HC08.pin6
  N53: R13.Pin_0, 74HC08.pin11
  N54: 74HC08.pin1, 74HC08.pin4, 74HC08.pin10, 74HC08.pin13, 74HC08_2.pin1, 74HC08_2.pin4, 74HC08_2.pin10, 74HC08_2.pin13, Z80.pin5, S19.COM, R51.Pin_1, R63.Pin_1
  N55: 74HC08.pin7, 74HC08_2.pin7, C6.0, C8.0
  N56: 74HC08.pin14, 74HC08_2.pin14, C6.1, C8.1
  N57: S3.COM, Z80.pin21, R24.Pin_1
  N58: Z80.pin16, R28.Pin_0
  N59: Z80.pin17, R27.Pin_0
  N60: Z80.pin18, R22.Pin_1
  N61: Z80.pin19, R23.Pin_1
  N62: Z80.pin24, R21.Pin_0
  N63: Z80.pin25, R20.Pin_0
  N64: Z80.pin26, R26.Pin_0, S5.COM
  N65: Z80.pin27, R19.Pin_1
  N66: R19.Pin_0, LED10.anode
  N67: R22.Pin_0, LED11.anode
  N68: R23.Pin_0, LED12.anode
  N69: R24.Pin_0, LED13.anode
  N70: R25.Pin_0, LED14.anode
  N71: S4.L1, R31.Pin_0
  N72: R33.Pin_0, LED15.anode
  N73: LED16.anode, R35.Pin_0
  N74: LED17.anode, R37.Pin_0
  N75: LED18.anode, R39.Pin_0
  N76: LED19.anode, R47.Pin_0
  N77: LED20.anode, R46.Pin_0
  N78: LED21.anode, R44.Pin_0
  N79: LED22.anode, R45.Pin_0
  N80: LED23.anode, R56.Pin_0
  N81: LED24.anode, R63.Pin_0
  N82: LED25.anode, R62.Pin_0
  N83: LED26.anode, R57.Pin_0
  N84: LED27.anode, R58.Pin_0
  N85: LED28.anode, R59.Pin_0
  N86: LED29.anode, R61.Pin_0
  N87: LED30.anode, R60.Pin_0
  N88: R65.Pin_0, R66.Pin_0, R67.Pin_0, R68.Pin_0, R69.Pin_0, R70.Pin_0, R71.Pin_0, R72.Pin_0
